# Fritzing sketch z-duino (saved by Fritzing 1.0.6)
breadboards: 1

parts:
  Part1 = Motor Driver 1A Dual TB6612FNG
  J3 = male pin header, 8 pins [form="♂ (male)"]
  J2 = male pin header, 8 pins [form="♂ (male)"]
  WeMos_D1_Mini1 = WeMos D1 Mini  # not connected
  J4 = single row smd male pin header, 8 pins [form="♂ (male)"]
  J5 = single row smd male pin header, 8 pins [form="♂ (male)"]
  Power_plug1 = Power plug

nets:
  N1: Part1.GND, J3.pin1, J2.pin1, J2.pin6
  N2: Part1.B01, J2.pin2
  N3: Part1.B02, J2.pin3
  N4: Part1.A02, J2.pin4
  N5: Part1.A01, J2.pin5
  N6: Part1.VCC, J2.pin7
  N7: Part1.VM, J2.pin8
  N8: Part1.PWMA, J3.pin8
  N9: Part1.AIN2, J3.pin7
  N10: Part1.AIN1, J3.pin6
  N11: Part1.STBY, J3.pin5
  N12: Part1.BIN1, J3.pin4
  N13: Part1.BIN2, J3.pin3
  N14: Part1.PWMB, J3.pin2
  N15: J4.pin1, J4.pin6, J5.pin1, Power_plug1.GND
  N16: J4.pin8, Power_plug1.VCC

notes:
  to rail A
  to rail B
